# Fritzing sketch Esquematico (saved by Fritzing 0.9.10b)
breadboards: 1

parts:
  A7670E = female pin header, 7 pins [form="♀ (female)"]
  Acc = STP16NF06 N-Channel Power MOSFET
  R3 = Resistor [tolerance=±5% resistance=1k power=0.25 package=THT]
  M1 = DOIT Esp32 DevKit v1 (30 pins long, 11 pins width) [part_number=ESP32S-PIN30]
  Bat1 = battery_holder_single_18650
  Bat2 = battery_holder_single_18650
  TP1 = TP4056 [chip_label=TP4056 package="DIP (Dual Inline) [THT]"]
  TFMini = female pin header, 4 pins [form="♀ (female)"]

nets:
  N1: A7670E.pin2, Acc.drain
  N2: A7670E.pin3, M1.VIN, TP1.pin3, TFMini.pin2
  N3: A7670E.pin5, M1.RX2
  N4: A7670E.pin6, M1.TX2
  N5: Acc.gate, R3.Pin_0, M1.D4
  N6: Acc.source, R3.Pin_1, M1.GND, TP1.pin6, TFMini.pin1
  N7: M1.D18, TFMini.pin4
  N8: M1.D19, TFMini.pin3
  N9: Bat1.+#0, TP1.pin5
  N10: Bat1.+#1, Bat2.+#0
  N11: Bat2.+#1, TP1.pin4

notes:
  0 S -- SLEEP
  1 G -- GND
  2 V -- VCC 5-10V
  3 K -- PWRKEY
  4 T -- TXD
  5 R -- RXD
  6 G -- GND
  GND
  5V
  RX
  TX

custom parts:
  STP16NF06 N-Channel Power MOSFET: STP16NF06 N-channel Power MOSFET
  DOIT Esp32 DevKit v1 (30 pins long, 11 pins width): The DOIT Esp32 DevKit v1 is one of the development board created by DOIT to evaluate the ESP-WROOM-32 module. It is based on the ESP32 microcontroller that boasts Wifi, Bluetooth, Ethernet and Low Power support all in a single chip. (vanepp) made breadboard work, adjusted pin numbering and labels and reduced size of schematic and cleaned up pcb. This chip is 30pins long (2 x15) and 11 pins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
  battery_holder_single_18650: single 18650 battery holder
  TP4056: A DIP stand-in part for whatever IC you want. With 6 pins on a 300mil dual inline package (DIP) footprint.
